# Fritzing sketch 01_Blinking_LED_part_A (saved by Fritzing 0.9.10b)
breadboards: 1

parts:
  Part1 = Arduino Nano (Rev3.0)
  breadboard = Resistor [tolerance=±5% power=0.25 resistance=220 package=THT]
  LED1 = LED - 3mm [color="Red (633nm)" current=0.030 package="3 mm [THT]"]

nets:
  N1: Part1.GND, LED1.cathode
  N2: Part1.D3, breadboard.Pin_0
  N3: breadboard.Pin_1, LED1.anode
