# Fritzing sketch 01_Blinking_LED_part_B (saved by Fritzing 0.9.10b)
breadboards: 1

parts:
  Part1 = Arduino Nano (Rev3.0)
  breadboard = Resistor [tolerance=±5% power=0.25 resistance=220 package=THT]
  S1 = Pushbutton [package="[SMD]"]
  LED1 = LED - 3mm [color="Red (633nm)" current=0.030 package="3 mm [THT]"]

nets:
  N1: Part1.GND, S1.Pin_3, S1.Pin_4, LED1.cathode
  N2: Part1.D3, breadboard.Pin_0
  N3: Part1.D5, S1.Pin_1, S1.Pin_2
  N4: breadboard.Pin_1, LED1.anode
